# Fritzing sketch sketch_circuito (saved by Fritzing 1.0.7)
stripboards: 1

parts:
  DC_Mot_Enc1 = DC Motor with two-phase hall-encoder [part_number=VT-E-G25A-06-177E]
  DC_Mot_Enc2 = DC Motor with two-phase hall-encoder [part_number=VT-E-G25A-06-177E]
  L298N1 = L298N DC motor driver
  A1 = Esp32-c3 super mini
  C1 = Electrolytic Capacitor [capacitance=1µF voltage=35V package="100 mil [THT, electrolytic]"]
  VCC1 = Battery [internal_resistance=0.1Ω]
  S1 = Round Pushbutton

nets:
  N1: DC_Mot_Enc1.pin1, L298N1.OUT1
  N2: DC_Mot_Enc1.pin2, L298N1.OUT2
  N3: DC_Mot_Enc1.pin3, A1.Pin_9
  N4: DC_Mot_Enc1.pin4, A1.Pin_10
  N5: DC_Mot_Enc1.pin5, DC_Mot_Enc2.pin5, A1.Pin_16, C1.+
  N6: DC_Mot_Enc1.pin6, DC_Mot_Enc2.pin6, L298N1.GND, A1.Pin_15, C1.-, VCC1.-
  N7: DC_Mot_Enc2.pin1, L298N1.OUT3
  N8: DC_Mot_Enc2.pin2, L298N1.OUT4
  N9: DC_Mot_Enc2.pin3, A1.Pin_11
  N10: DC_Mot_Enc2.pin4, A1.Pin_12
  N11: L298N1.12V, S1.leg1
  N12: L298N1.ENA, A1.Pin_13
  N13: L298N1.ENB, A1.Pin_3
  N14: L298N1.IN1, A1.Pin_1
  N15: L298N1.IN2, A1.Pin_2
  N16: L298N1.IN3, A1.Pin_5
  N17: L298N1.IN4, A1.Pin_4
  N18: VCC1.+, S1.leg0

custom parts:
  L298N DC motor driver: 2x DC motor driver with 78M05 positive voltage regulator (7..35 V) L298N: max 46 V, 2 A Set 5 V Enable jumper to enable 5 V regultor (needed for the L298N) and +5 V output at screw terminal or supply external +5 V at screw terminal Set ENA and/or ENB to +5 V to enable motor permanently or supply ENA and/or ENB with PWM signal IN1 and IN2 set rotation directory for motor A (OUT1/OUT2) IN2 and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
  Esp32-c3 super mini: ESP32-C3 Development Board ESP32 SuperMini Development Board ESP32 Development Board WiFi Bluetooth.
